# Fritzing sketch schematic (saved by Fritzing 0.9.4)
breadboards: 1

parts:
  Part1 = Arduino Micro (Rev3)  # not connected
  S1 = Pushbutton [package="[THT]"]
  LED1 = RGB LED (com. cathode, rgb) [package="5 mm [THT]"]  # not connected

nets:
  N1: S1.Pin_1, S1.Pin_2
  N2: S1.Pin_3, S1.Pin_4
